# Fritzing sketch seminario (saved by Fritzing 0.8.5b)
breadboards: 1

parts:
  Parte1 = Arduino Uno (Rev3)
  R1 = Trimmer Potentiometer [maximum_resistance=10kΩ package=THT]
  R2 = Trimmer Potentiometer [maximum_resistance=10kΩ package=THT]
  LCD1 = LCD screen

nets:
  N1: Parte1.A5/SCL, R1.wiper
  N2: Parte1.D2, LCD1.DB7
  N3: Parte1.D3_PWM, LCD1.DB6
  N4: Parte1.D4, LCD1.DB5
  N5: Parte1.D5_PWM, LCD1.DB4
  N6: Parte1.D6_PWM, LCD1.E
  N7: Parte1.D7, LCD1.RS
  5V: Parte1.5V, R1.leg1, R2.leg1, LCD1.VDD, LCD1.LED+
  GND: Parte1.GND, R1.leg2, R2.leg2, LCD1.VSS, LCD1.R/W, LCD1.LED-
  N8: R2.wiper, LCD1.V0
